# Fritzing sketch trinket with switch and leds (saved by Fritzing 0.9.3b)
breadboards: 1

parts:
  Part1 = Adafruit Trinket 5V
  Q1 = NPN-Transistor [package="TO92 [THT]"]
  Q2 = NPN-Transistor [package="TO92 [THT]"]
  R1 = Resistor [tolerance=±5% resistance=220 package=THT]
  R2 = Resistor [tolerance=±5% resistance=220 package=THT]
  R3 = Resistor [tolerance=±5% resistance=220 package=THT]
  S1 = Toggle Switch [package=THT]
  LED1 = LED - 5mm [color="White (6500K)" package="5 mm [THT]"]
  LED2 = LED - 5mm [color="White (6500K)" package="5 mm [THT]"]
  LED3 = LED - 5mm [color="White (6500K)" package="5 mm [THT]"]

nets:
  N1: Part1.VBAT, LED1.cathode
  GND: Part1.GND, Q1.E, Q2.E, S1.L2
  N2: Part1.#1, Q2.B
  N3: Part1.#0, Q1.B
  N4: Q1.C, LED2.cathode
  N5: Q2.C, LED3.cathode
  N6: R1.Pin_0, S1.L1
  N7: R1.Pin_1, LED1.anode
  12V: R2.Pin_0, R3.Pin_0, S1.COM
  N8: R2.Pin_1, LED2.anode
  N9: R3.Pin_1, LED3.anode

custom parts:
  Adafruit Trinket 5V: Trinket may be small, but do not be fooled by its size! It's a tiny microcontroller board, built around the Atmel ATtiny85, a little chip with a lot of power. We wanted to design a microcontroller board that was small enough to fit into any project, and low cost enough to use without hesitation. Perfect for when you don't want to give up your expensive dev-board and you aren't willing to take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
