# Fritzing sketch rpi and display (saved by Fritzing 0.9.3b)
breadboards: 1

parts:
  MCU1 = Raspberry Pi Zero
  U1 = LCD-16X2 [package=lcd-8x2-kit]
  U2 = POT [package=alps_pot]
  S1 = Round Pushbutton
  S2 = Round Pushbutton

nets:
  5V: MCU1.pin_2, U1.VDD, U1.A, U2.E
  GND: MCU1.pin_6, MCU1.pin_25, MCU1.pin_34, MCU1.pin_39, U1.VSS, U1.R_W, U1.DB4, U1.K, U2.A, S1.leg0, S2.leg0
  N1: MCU1.pin_12, S2.leg1
  N2: MCU1.pin_18, U1.DB7
  N3: MCU1.pin_22, U1.E
  N4: MCU1.pin_23, U1.DB6
  N5: MCU1.pin_24, U1.DB5
  N6: MCU1.pin_26, S1.leg1
  N7: MCU1.pin_27, U1.RS
  N8: U1.VO, U2.S
